// Logisim project lab5.circ as structural Verilog
module FullAdder (
  input  a,
  input  b,
  input  c_in,
  output sum,
  output c_out
);

  wire and_1_out, and_2_out, xor_1_out;

  xor xor_1 (xor_1_out, a, b);
  and and_1 (and_1_out, xor_1_out, c_in);
  and and_2 (and_2_out, b, a);
  xor xor_2 (sum, xor_1_out, c_in);
  or or_1 (c_out, and_1_out, and_2_out);
endmodule

module FullAdder4Bit (
  input  [3:0] a,
  input  [3:0] b,
  input  c_in,
  output [3:0] sum,
  output c_out
);

  wire fulladder_1_c_out, fulladder_2_c_out, fulladder_3_c_out;

  FullAdder fulladder_1 (.a(a[0]), .b(b[0]), .c_in(c_in), .sum(sum[0]), .c_out(fulladder_1_c_out));
  FullAdder fulladder_2 (.a(a[1]), .b(b[1]), .c_in(fulladder_1_c_out), .sum(sum[1]), .c_out(fulladder_2_c_out));
  FullAdder fulladder_3 (.a(a[2]), .b(b[2]), .c_in(fulladder_2_c_out), .sum(sum[2]), .c_out(fulladder_3_c_out));
  FullAdder fulladder_4 (.a(a[3]), .b(b[3]), .c_in(fulladder_3_c_out), .sum(sum[3]), .c_out(c_out));

  // Other names for the same wires on the sheet: s0 = sum[0]; s1 = sum[1]; s2 = sum[2]; s3 = sum[3]

  // Notes on the sheet:
  //   Inputs
  //   Outputs
endmodule

module DFlipFlop (
  input  D,
  output Q,
  output Q_inv
);

  wire nand_1_out, nand_2_out, not_1_out, R_out;

  Clock R (.out(R_out));
  not not_1 (not_1_out, D);
  nand nand_1 (nand_1_out, D, R_out);
  nand nand_2 (nand_2_out, R_out, not_1_out);
  nand nand_3 (Q, nand_1_out, Q_inv);
  nand nand_4 (Q_inv, Q, nand_2_out);
endmodule

module TFlipFlop (
  output c_0,
  output c_1,
  output c_2,
  output c_3
);

  wire clock_1_out, d_ff_1_qn, d_ff_2_qn, d_ff_3_qn, d_ff_4_qn;

  D_Flip_Flop d_ff_1 (.D(d_ff_1_qn), .clk(clock_1_out), .Q(c_0), .Qn(d_ff_1_qn));  // open: preset, reset
  Clock clock_1 (.out(clock_1_out));
  D_Flip_Flop d_ff_2 (.D(d_ff_2_qn), .clk(d_ff_1_qn), .Q(c_1), .Qn(d_ff_2_qn));  // open: preset, reset
  D_Flip_Flop d_ff_3 (.D(d_ff_3_qn), .clk(d_ff_2_qn), .Q(c_2), .Qn(d_ff_3_qn));  // open: preset, reset
  D_Flip_Flop d_ff_4 (.D(d_ff_4_qn), .clk(d_ff_3_qn), .Q(c_3), .Qn(d_ff_4_qn));  // open: preset, reset
endmodule
